// Logisim project 21.circ as structural Verilog: 2 circuits, main circuit main
module main (
  input  x,
  input  y,
  input  z,
  output out_4,
  output out_5,
  output out_6,
  output out_7,
  output out_8,
  output out_9,
  output out_10,
  output out_11
);

  wire not_1_out, not_2_out, not_3_out;

  not not_1 (not_1_out, y);
  not not_2 (not_2_out, z);
  not not_3 (not_3_out, x);
  and and_1 (out_4, not_3_out, not_1_out, not_2_out);
  and and_2 (out_5, not_3_out, not_1_out, z);
  and and_3 (out_6, y, not_2_out);
  and and_4 (out_7, not_3_out, y, z);
  and and_5 (out_8, x, not_1_out, not_2_out);
  and and_6 (out_9, x, not_1_out, z);
  and and_7 (out_10, x, y, not_2_out);
  and and_8 (out_11, x, y, z);

  // Notes on the sheet:
  //   3-8译码器
endmodule

module m (
  input  x,
  input  y,
  output x_y,
  output x_y_2,
  output x_y_3
);

  wire and_1_out, not_1_out, or_1_out;

  not not_1 (not_1_out, and_1_out);
  and and_1 (and_1_out, x, y);
  and and_2 (x_y, x, not_1_out);
  and and_3 (x_y_3, not_1_out, y);
  or or_1 (or_1_out, x_y, x_y_3);
  not not_2 (x_y_2, or_1_out);

  // Notes on the sheet:
  //   一位二进制比较器
  //   一位二进制比较器
endmodule
