// Logisim project 1.circ as structural Verilog
module test4 (
  input  a,
  input  b,
  input  c,
  input  d,
  input  e,
  input  f,
  input  g,
  input  h,
  input  x2,
  output x,
  output y,
  output z,
  output u,
  output v
);

  or or_1 (x, c, b, a);
  or or_2 (y, e, d, c, b, a);
  or or_3 (z, h, g, e, d, c, b, a);
  or or_4 (u, x2, h, g, f, e, d, c, b, a);
  or or_5 (v, x2, h, g, f, e, d, c, b, a);

  // Notes on the sheet:
  //   四位串行加法器
endmodule

module test2 (
  input  A,
  input  B,
  input  C,
  output O1,
  output O2
);

  wire and_1_out, and_2_out, and_3_out;

  and and_1 (and_1_out, B, C);
  and and_2 (and_2_out, A, C);
  and and_3 (and_3_out, A, B);
  or or_1 (O2, C, B, A);
  or or_2 (O1, and_1_out, and_2_out, and_3_out);
endmodule
