// Logisim project 2.circ as structural Verilog: 1 circuit, main circuit main
module main (
  input  A3,
  input  B3,
  input  A2,
  input  B2,
  input  A1,
  input  B1,
  input  A0,
  input  B0,
  input  C0,
  output C4,
  output S3,
  output C3,
  output S2,
  output C2,
  output S1,
  output C1,
  output S0
);

  wire and_1_out, and_2_out, and_3_out, and_4_out, and_5_out, and_6_out, and_7_out, and_8_out, and_9_out,
       and_10_out, and_11_out, and_12_out, and_13_out, and_14_out, or_1_out, or_2_out, or_3_out, or_4_out;

  and and_1 (and_1_out, A3, B3);
  or or_1 (or_1_out, B3, A3);
  and and_2 (and_2_out, A2, B2);
  or or_2 (or_2_out, B2, A2);
  and and_3 (and_3_out, A1, B1);
  or or_3 (or_3_out, B1, A1);
  and and_4 (and_4_out, A0, B0);
  or or_4 (or_4_out, B0, A0);
  and and_5 (and_5_out, or_1_out, or_2_out, and_3_out);
  and and_6 (and_6_out, or_1_out, and_3_out, or_3_out, and_4_out);
  and and_7 (and_7_out, or_1_out, or_2_out, or_3_out, or_4_out, C0);
  and and_8 (and_8_out, or_2_out, and_3_out);
  and and_9 (and_9_out, or_2_out, or_3_out, and_4_out);
  and and_10 (and_10_out, or_2_out, or_3_out, or_4_out, C0);
  and and_11 (and_11_out, or_3_out, and_4_out);
  and and_12 (and_12_out, or_3_out, or_4_out, C0);
  and and_13 (and_13_out, or_4_out, C0);
  and and_14 (and_14_out, or_1_out, and_2_out);
  or or_5 (C3, and_2_out, and_8_out, and_9_out, and_10_out);
  or or_6 (C2, and_3_out, and_11_out, and_12_out);
  or or_7 (C1, and_4_out, and_13_out);
  or or_8 (C4, and_1_out, and_14_out, and_5_out, and_6_out, and_7_out);
  or or_9 (S3, or_1_out, C3);
  or or_10 (S2, or_2_out, C2);
  or or_11 (S1, or_3_out, C1);
  or or_12 (S0, or_4_out, C0);

  // Notes on the sheet:
  //   四位并行加法器
endmodule
